// Logisim project ALU.circ as structural Verilog: 9 circuits, main circuit 1bit_adder
module xor_gate (
  input  A,
  input  B,
  output Output
);

  wire and_1_out, and_2_out, not_1_out, not_2_out;

  not not_1 (not_1_out, A);
  not not_2 (not_2_out, B);
  and and_1 (and_1_out, A, not_2_out);
  and and_2 (and_2_out, not_1_out, B);
  or or_1 (Output, and_1_out, and_2_out);

  // Notes on the sheet:
  //   Section 1.1 简单异或门的实现
  //   可以尝试修改输入A,B的值来观察输出的变化
  //   这里给出了一个非常简单的异或门的实现，A和B都是输入信号，Output都是输出信号
endmodule

module xor_gate_use (
  input  in_1,
  input  in_2,
  output out_3
);

  xor_gate \u_自定义的异或门  (.A(in_1), .B(in_2), .Output(out_3));

  // Notes on the sheet:
  //   Section 1.2 简单异或门的使用
  //   可以尝试修改输入的值来观察输出的变化
  //   在Sectino1.1中我们实现了一个简单异或门，其中A和B都是输入信号，Output都是输出信号。
  //   这样我们就可以在其它电路设计中，直接使用我们设计好的异或门，这就是模块化设计。
endmodule

module _1bit_adder (
  input  A,
  input  B,
  input  Cin,
  output S,
  output Cout
);

  wire and_1_out, and_2_out, xor_gate_1_output;

  xor_gate xor_gate_1 (.A(A), .B(B), .Output(xor_gate_1_output));
  xor_gate xor_gate_2 (.A(xor_gate_1_output), .B(Cin), .Output(S));
  and and_1 (and_1_out, xor_gate_1_output, Cin);
  and and_2 (and_2_out, A, B);
  or or_1 (Cout, and_1_out, and_2_out);

  // Notes on the sheet:
  //   Section 2. 通过基础门电路实现1位全加器
  //   1-Bit 全加器
  //   使用Section 1中实现的异或门，以及自带的与门和或门，体会模块化设计
  //   A和B分别代表1位的加数，Cin(Carry in) 代表低位的进位输入。S(Sum)代表当前为的和，Cout(Carry out)代表向高位的进位输出
endmodule

module _4bit_adder (
  input  Cin,
  input  [3:0] A,
  input  [3:0] B,
  output [3:0] S,
  output Cout
);

  wire n1bit_adder_1_cout, n1bit_adder_2_cout, n1bit_adder_3_cout;

  _1bit_adder u_1bit_adder_1 (.A(A[0]), .B(B[0]), .Cin(Cin), .S(S[0]), .Cout(n1bit_adder_1_cout));
  _1bit_adder u_1bit_adder_2 (.A(A[1]), .B(B[1]), .Cin(n1bit_adder_1_cout), .S(S[1]), .Cout(n1bit_adder_2_cout));
  _1bit_adder u_1bit_adder_3 (.A(A[2]), .B(B[2]), .Cin(n1bit_adder_2_cout), .S(S[2]), .Cout(n1bit_adder_3_cout));
  _1bit_adder u_1bit_adder_4 (.A(A[3]), .B(B[3]), .Cin(n1bit_adder_3_cout), .S(S[3]), .Cout(Cout));

  // Notes on the sheet:
  //   Section 3. 四位全加器的实现
  //   利用Section 2中的一位全加器，我们可以轻松实现四位全加器
  //   A0+B0
  //   在Logisim中，要提取出四位输入中的各个位置的数值，需要使用到Wiring下的Spitter来拆分多位数值
  //   A1+B1
  //   A2+B2
  //   A3+B3
endmodule

module reverse_and_add_1 (
  input  [3:0] Input,
  output [3:0] Output,
  output Cout
);

  wire [3:0] not_1_out;

  not not_1 (not_1_out[0], Input[0]);
  not not_2 (not_1_out[1], Input[1]);
  not not_3 (not_1_out[2], Input[2]);
  not not_4 (not_1_out[3], Input[3]);
  _4bit_adder u_4bit_adder_1 (.Cin(1'b0), .A(not_1_out), .B(4'b0001), .S(Output), .Cout(Cout));

  // Notes on the sheet:
  //   Section 4. 补码操作实现
  //   该部分需要实现的逻辑就是将Input取反再加一
  //   思考：如果对正数进行了取反再加一的操作，得到的数是什么？
  //   需要注意的是，这不是严格的对任意数取补码的操作，因为对于正数来说原码就是其补码，无需取反加一
endmodule

// Sub
module _4bit_sub (
  input  Bin,
  input  [3:0] A,
  input  [3:0] B,
  output [3:0] S,
  output Bout
);

  wire _4bit_adder_cout;
  wire [3:0] \补码器_output ;

  reverse_and_add_1 \u_补码器  (.Input(B), .Output(\补码器_output ));  // open: Cout
  _4bit_adder _4bit_adder (.Cin(Bin), .A(A), .B(\补码器_output ), .S(S), .Cout(_4bit_adder_cout));
  not not_1 (Bout, _4bit_adder_cout);

  // Notes on the sheet:
  //   Section 5. 减法器实现
  //   实现A-B的四位减法器，Bin代表下一级的借位信号
  //   思考是不是要用到补码器？从逻辑表达式的角度出发！
  //   这里的Bout(Borrow out)代表借位输出，小减大时该信号应该为1，表示发生了借位。
endmodule

module MUX (
  input  [3:0] Input3,
  input  [3:0] Input2,
  input  [3:0] Input1,
  input  [3:0] Input0,
  input  [1:0] S,
  output [3:0] Y
);

  wire _00_out, _01_out, _10_out, _11_out, and_1_out, and_2_out, and_3_out, and_4_out, not_1_out, not_2_out;

  not not_1 (not_1_out, S[0]);
  not not_2 (not_2_out, S[1]);
  and _11 (_11_out, S[0], S[1]);
  and _10 (_10_out, not_1_out, S[1]);
  and _01 (_01_out, S[0], not_2_out);
  and _00 (_00_out, not_1_out, not_2_out);
  and and_1 (and_1_out, Input3[0], _11_out);
  and and_2 (and_2_out, Input2[0], _10_out);
  and and_3 (and_3_out, Input1[0], _01_out);
  and and_4 (and_4_out, Input0[0], _00_out);
  // AND_Gate and_5 has open pins: in0=Input3[1], out=open
  // AND_Gate and_6 has open pins: in0=Input2[1], out=open
  // AND_Gate and_7 has open pins: in0=Input1[1], out=open
  // AND_Gate and_8 has open pins: in0=Input0[1], in1=_00_out, out=open
  // OR_Gate or_1 has open pins: in0=and_1_out, in1=and_2_out, in2=and_3_out, in3=and_4_out, out=open
  // AND_Gate and_9 is placed but not wired
  // AND_Gate and_10 is placed but not wired
  // AND_Gate and_11 is placed but not wired
  // AND_Gate and_12 is placed but not wired
  // OR_Gate or_2 is placed but not wired
  // AND_Gate and_13 is placed but not wired
  // AND_Gate and_14 is placed but not wired
  // AND_Gate and_15 is placed but not wired
  // AND_Gate and_16 is placed but not wired

  // Notes on the sheet:
  //   Section 6.四选一多路选择器设计
  //   Y输出信号（4位）
  //   第0位
  //   上回划到这了！
  //   Input0和Input1代表数据输入（4位），S选择信号（2位），00代表选择Input0，01代表选择Input1，10代表选择Input2，11代表选择Input3
  //   Tips：根据不同的实现方案，你也许会需要使用到Wiring下的Bit Extender或者Splitter
  //   第1位
  //   第2位
  //   第2位
endmodule

module ALU (
  input  Cin,
  input  [3:0] A,
  input  [3:0] B,
  input  [1:0] S,
  output [3:0] Ans,
  output Xout
);


  // Notes on the sheet:
  //   Section 7. ALU设计
  //   S为00时代表加法，01代表减法，10代表与，11代表或
  //   将之前设计的加法器、减法器，以及Logisim提供的4位与和或通过多路选择器组合起来，得到一个非常简单的ALU模块
  //   A和B分别第一个输入和第二个输入，运算顺序位A op B。Cin(Carry in) 代表低位的进位输入。Ans代表当前运算结果，Xout代表向高位的进位或借位输出
endmodule

module main (
  input  Xin,
  input  [3:0] A,
  input  [3:0] B,
  input  [1:0] S,
  output [3:0] Ans,
  output Xout
);

  ALU alu_1 (.Cin(Xin), .A(A), .B(B), .S(S), .Ans(Ans), .Xout(Xout));

  // Notes on the sheet:
  //   Final Section
  //   验收部分，确保你的ALU模块准确无误
endmodule
