// Logisim project 1fa.circ as structural Verilog: 5 circuits, main circuit main
module main (
  input  A,
  input  B,
  input  Cin,
  output S,
  output Carry
);

  wire and_1_out, and_2_out, xor_1_out;

  xor xor_1 (xor_1_out, A, B);
  xor xor_2 (S, xor_1_out, Cin);
  and and_1 (and_1_out, Cin, xor_1_out);
  and and_2 (and_2_out, B, A);
  or or_1 (Carry, and_1_out, and_2_out);
endmodule

module _1fa (
  input  A,
  input  B,
  input  Cin,
  output S,
  output Carry
);

  wire and_1_out, and_2_out, xor_1_out;

  xor xor_1 (xor_1_out, A, B);
  xor xor_2 (S, xor_1_out, Cin);
  and and_1 (and_1_out, Cin, xor_1_out);
  and and_2 (and_2_out, B, A);
  or or_1 (Carry, and_1_out, and_2_out);
endmodule

module _4fa (
  input  A3,
  input  B3,
  input  A2,
  input  B2,
  input  A1,
  input  B1,
  input  A0,
  input  B0,
  input  Cin,
  output S3,
  output Cout3,
  output S2,
  output S1,
  output S0
);

  wire and_1_out, and_2_out, and_3_out, and_4_out, and_5_out, and_6_out, and_7_out, and_8_out, or_2_out,
       or_3_out, or_4_out, xor_1_out, xor_2_out, xor_3_out, xor_4_out;

  xor xor_1 (xor_1_out, A3, B3);
  xor xor_2 (xor_2_out, A2, B2);
  xor xor_3 (xor_3_out, A1, B1);
  xor xor_4 (xor_4_out, A0, B0);
  xor xor_5 (S3, xor_1_out, or_2_out);
  and and_1 (and_1_out, or_2_out, xor_1_out);
  and and_2 (and_2_out, B3, A3);
  xor xor_6 (S2, xor_2_out, or_3_out);
  and and_3 (and_3_out, or_3_out, xor_2_out);
  and and_4 (and_4_out, B2, A2);
  xor xor_7 (S1, xor_3_out, or_4_out);
  and and_5 (and_5_out, or_4_out, xor_3_out);
  and and_6 (and_6_out, B1, A1);
  xor xor_8 (S0, xor_4_out, Cin);
  and and_7 (and_7_out, Cin, xor_4_out);
  and and_8 (and_8_out, B0, A0);
  or or_1 (Cout3, and_1_out, and_2_out);
  or or_2 (or_2_out, and_3_out, and_4_out);
  or or_3 (or_3_out, and_5_out, and_6_out);
  or or_4 (or_4_out, and_7_out, and_8_out);
endmodule

module comp (
);

  wire multiplexer_1_out, undriven;

  // NOT_Gate not_1 is placed but not wired
  // NOT_Gate not_2 is placed but not wired
  // NOT_Gate not_3 is placed but not wired
  // NOT_Gate not_4 is placed but not wired
  Multiplexer #(.select(1), .width(1), .disabled("Z"), .enable("false")) multiplexer_1 (
    .out(multiplexer_1_out), .sel(undriven));  // open: in0, in1
endmodule

module _4_1mux (
  input  A0,
  input  A1,
  input  D3,
  input  D2,
  input  D1,
  input  D0,
  output Y
);

  wire and_1_out, and_2_out, and_3_out, and_4_out, and_5_out, and_6_out, and_7_out, and_8_out, not_1_out,
       not_2_out, not_3_out, not_4_out, or_1_out, or_2_out;

  not not_1 (not_1_out, A0);
  not not_2 (not_2_out, not_1_out);
  not not_3 (not_3_out, A1);
  not not_4 (not_4_out, not_3_out);
  and and_1 (and_1_out, not_4_out, not_2_out);
  and and_2 (and_2_out, not_4_out, not_1_out);
  and and_3 (and_3_out, not_3_out, not_2_out);
  and and_4 (and_4_out, not_3_out, not_1_out);
  and and_5 (and_5_out, and_1_out, D3);
  and and_6 (and_6_out, and_2_out, D2);
  and and_7 (and_7_out, and_3_out, D1);
  and and_8 (and_8_out, and_4_out, D0);
  or or_1 (or_1_out, and_5_out, and_6_out);
  or or_2 (or_2_out, and_7_out, and_8_out);
  or or_3 (Y, or_1_out, or_2_out);
endmodule
